# Fritzing sketch ch_02_Flasher (saved by Fritzing 0.8.7b)
circuit board: 5cm x 4cm
breadboards: 1

parts:
  IC1 = General purpose bipolar Timer [package=dil-08]
  R1 = Resistor [tolerance=±5% resistance=1k package=THT]
  R2 = Resistor [tolerance=±5% resistance=470k package=THT]
  R3 = Resistor [tolerance=±5% resistance=220 package=THT]
  R4 = Resistor [tolerance=±5% resistance=220 package=THT]
  C1 = Electrolytic Capacitor [capacitance=1µF package="100 mil [THT, electrolytic]"]
  C2 = Ceramic Capacitor [capacitance=100nF package="100 mil [THT, multilayer]"]
  LED1 = LED - 5mm [color="Red (633nm)" package="5 mm [THT]"]
  LED2 = LED - 5mm [color="Red (633nm)" package="5 mm [THT]"]
  part = Battery block 9V

nets:
  N1: IC1.GND, C1.-, C2.0, LED1.cathode, part.-
  N2: IC1.TRI, IC1.TRE, R2.Pin_0, C1.+
  N3: IC1.OUT, R3.Pin_0, R4.Pin_1
  N4: IC1._RES, IC1.VCC+, R1.Pin_1, LED2.anode, part.+
  N5: IC1.CON, C2.1
  N6: IC1.DIS, R1.Pin_0, R2.Pin_1
  N7: R3.Pin_1, LED2.cathode
  N8: R4.Pin_0, LED1.anode
