# Fritzing sketch ch_03_Musical_Instrument (saved by Fritzing 0.8.7b)
breadboards: 1

parts:
  Part1 = Arduino Uno (Rev3) - ICSP
  AMP1 = MAX98306_Stereo_Amplifier
  SP1 = SPEAKER [package=pcb_mount_speaker]
  U2 = HC-SR04 [chip_label=IC package="SIP (Single Inline) [THT]"]
  POT1 = Breadboard Trimpot
  R1 = Resistor [tolerance=±5% resistance=10k package=THT]

nets:
  N1: Part1.D9_PWM, R1.Pin_1
  N2: Part1.D11_PWM/MOSI, U2.Trig
  N3: Part1.D12/MISO, U2.Echo
  GND: Part1.GND, AMP1.connector1, U2.GND, POT1.PIN3
  5V: Part1.5V, AMP1.connector2, AMP1.connector5, AMP1.connector6, AMP1.connector7, U2.Vcc
  N4: AMP1.connector4, POT1.PIN2
  N5: AMP1.connector10, SP1.+
  N6: AMP1.connector11, SP1.-
  N7: POT1.PIN1, R1.Pin_0

custom parts:
  HC-SR04: HC-SR04 ultrasound distance sensor
