# Fritzing sketch ch_03_Shrimping (saved by Fritzing 0.8.7b)
breadboards: 1

parts:
  AMP1 = MAX98306_Stereo_Amplifier
  SP1 = SPEAKER [package=pcb_mount_speaker]
  U2 = HC-SR04 [chip_label=IC package="SIP (Single Inline) [THT]"]
  POT1 = Breadboard Trimpot
  R1 = Resistor [tolerance=±5% resistance=10k package=THT]
  U3 = atmega328 [package=dip]
  XTAL1 = Crystal [frequency="16 Mhz" package=SMD]
  C1 = Ceramic Capacitor [capacitance=100nF package="200 mil [THT, multilayer]"]
  C2 = Ceramic Capacitor [capacitance=100nF package="200 mil [THT, multilayer]"]
  IC1 = Voltage Regulator [package=78xxl]
  BAT1 = BC9VPC [package=bc9vpc]
  C3 = Electrolytic Capacitor [capacitance=10μF package="0605 [SMD, electrolytic]"]
  C4 = Ceramic Capacitor [capacitance=100nF package="200 mil [THT, multilayer]"]

nets:
  VCC: AMP1.connector1, U2.Vcc, U3.VCC, IC1.OUT, C3.-, C4.0
  GND: AMP1.connector2, AMP1.connector5, AMP1.connector6, AMP1.connector7, U2.GND, POT1.PIN3, U3.GND#7, C1.0, C2.1, IC1.GND, BAT1.V+, C3.+, C4.1
  N1: AMP1.connector4, POT1.PIN2
  N2: AMP1.connector10, SP1.+
  N3: AMP1.connector11, SP1.-
  N4: U2.Trig, U3.D11_(PWM)
  N5: U2.Echo, U3.D12
  N6: POT1.PIN1, R1.Pin_0
  N7: R1.Pin_1, U3.D9_(PWM)
  N8: U3.XLAT1, XTAL1.pin_0, C1.1
  N9: U3.XLAT2, XTAL1.pin_1, C2.0
  N10: IC1.IN, BAT1.V-

custom parts:
  HC-SR04: HC-SR04 ultrasound distance sensor
