# Fritzing sketch ch_04_2N3904 (saved by Fritzing 0.9.1b)
breadboards: 1

parts:
  Part1 = Arduino Uno (Rev3) - ICSP
  R1 = Resistor [tolerance=±5% resistance=270 package=THT]
  Motor = DC Motor
  Q1 = NPN-Transistor [part_number=2N3904 package="TO92 [THT]"]
  9V_Battery = 4 x AAA Battery Mount
  D1 = Diode [package=diode-1n4001]
  TP1 = TEST-POINT [package=pad.03x.05]

nets:
  N1: Part1.ICSP_MOSI, Part1.D11_PWM/MOSI, R1.Pin_0, TP1.1
  N2: Part1.GND, Q1.E, 9V_Battery.-
  N3: R1.Pin_1, Q1.B
  N4: Motor.pin_1, 9V_Battery.+, D1.C
  N5: Motor.pin_2, Q1.C, D1.A

notes:
  base
  emitter
  collector
