# Fritzing sketch ch_04_FQP30N06 (saved by Fritzing 0.8.7b)
breadboards: 1

parts:
  Part1 = Arduino Uno (Rev3) - ICSP
  R1 = Resistor [tolerance=±5% resistance=270 package=THT]
  VCC1 = 4 x AAA Battery Mount
  Q1 = Basic FET N-Channel [package="TO220 [THT]"]
  M1 = DC Motor

nets:
  N1: Part1.ICSP_MOSI, Part1.D11_PWM/MOSI, R1.Pin_0
  N2: Part1.GND, VCC1.-, Q1.source
  N3: R1.Pin_1, Q1.gate
  N4: VCC1.+, M1.pin_1
  N5: Q1.drain, M1.pin_2
