# Fritzing sketch ch_04_Push_Switch (saved by Fritzing 0.8.7b)
breadboards: 1

parts:
  LED1 = smd LED [color="Red (633nm)" package="0603 [SMD]"]
  R1 = Resistor [tolerance=±5% resistance=470 package=THT]
  S1 = Pushbutton [package="[THT]"]
  VCC1 = Battery block 9V

nets:
  N1: LED1.cathode, VCC1.-
  N2: LED1.anode, R1.Pin_1
  N3: R1.Pin_0, S1.Pin_3, S1.Pin_4
  N4: S1.Pin_1, S1.Pin_2, VCC1.+
