# Fritzing sketch ch_04_RGB_LED (saved by Fritzing 0.8.7b)
breadboards: 1

parts:
  BAT1 = BC9VPC [package=bc9vpc]
  R1 = Resistor [tolerance=±5% resistance=470 package=THT]
  LED1 = RGB LED (com. cathode, rbg) [package="5 mm [THT]"]
  R2 = Resistor [tolerance=±5% resistance=470 package=THT]
  R3 = Resistor [tolerance=±5% resistance=470 package=THT]

nets:
  N1: BAT1.V+, LED1.common_cathode
  N2: BAT1.V-, R1.Pin_0, R2.Pin_0, R3.Pin_0
  N3: R1.Pin_1, LED1.red_anode
  N4: LED1.blue_anode, R2.Pin_1
  N5: LED1.green_anode, R3.Pin_1
