# Fritzing sketch ch_04_Resistor_LED (saved by Fritzing 0.8.7b)
breadboards: 1

parts:
  BAT1 = BC9VPC [package=bc9vpc]
  LED1 = smd LED [color="Red (633nm)" package="0603 [SMD]"]
  R1 = Resistor [tolerance=±5% resistance=470 package=THT]

nets:
  N1: BAT1.V+, LED1.cathode
  N2: BAT1.V-, R1.Pin_0
  N3: LED1.anode, R1.Pin_1
