# Fritzing sketch ch_04_Slide_Switch (saved by Fritzing 0.8.7b)
breadboards: 1

parts:
  LED1 = smd LED [color="Red (633nm)" package="0603 [SMD]"]
  R1 = Resistor [tolerance=±5% resistance=470 package=THT]
  S1 = Toggle Switch [package=THT]
  Battery = Battery block 9V

nets:
  N1: LED1.cathode, Battery.-
  N2: LED1.anode, R1.Pin_1
  N3: R1.Pin_0, S1.L2
  N4: S1.COM, Battery.+
