# Fritzing sketch ch_05_Net_Labels (saved by Fritzing 0.8.7b)
breadboards: 1

parts:
  Part1 = Arduino Pro Mini v13
  Q1 = NPN-Transistor [package="TO92 [THT]"]
  M1 = DC Motor
  D1 = Rectifier Diode [part_number=1N4001 package="300 mil [THT]"]
  R1 = Resistor [tolerance=±5% resistance=220 package=THT]

nets:
  GND: Part1.GND, Q1.E
  5V: Part1.VCC
  D9: Part1.D9_PWM, R1.Pin_0
  N1: Q1.B, R1.Pin_1
  N2: Q1.C, M1.pin_2, D1.anode
  12V: M1.pin_1, D1.cathode
