# Fritzing sketch ch_06_PCB_Shape (saved by Fritzing 0.9.1b)
circuit board: 10.571cm x 10.571cm
breadboards: 1

parts:
  LED1 = LED - 5mm [color="Red (633nm)" package="5 mm [THT]"]
  BAT1 = BC9VPC [package=bc9vpc]
  S1 = Toggle Switch [package=THT]
  LED2 = LED - 5mm [color="Red (633nm)" package="5 mm [THT]"]
  LED3 = LED - 5mm [color="Red (633nm)" package="5 mm [THT]"]
  LED4 = LED - 5mm [color="Red (633nm)" package="5 mm [THT]"]
  LED5 = LED - 5mm [color="Red (633nm)" package="5 mm [THT]"]

nets:
  N1: LED1.cathode, LED2.anode
  N2: LED1.anode, S1.L2
  N3: BAT1.V+, S1.COM
  N4: BAT1.V-, LED5.cathode
  N5: LED2.cathode, LED3.anode
  N6: LED3.cathode, LED4.anode
  N7: LED4.cathode, LED5.anode
