# Fritzing sketch ch_08_Arduino_Nano (saved by Fritzing 0.8.7b)
breadboards: 1

parts:
  Part1 = Arduino Nano (Rev3.0)
  R1 = Resistor [tolerance=±5% resistance=220 package=THT]
  LED1 = LED - 5mm [color="Red (633nm)" package="5 mm [THT]"]

nets:
  N1: Part1.GND, LED1.cathode
  N2: Part1.D3, R1.Pin_0
  N3: R1.Pin_1, LED1.anode
