# Fritzing sketch ch_08_Arduino_baseline (saved by Fritzing 0.9.1b)
circuit board: 5.0223cm x 4.33335cm
breadboards: 1

parts:
  IC1 = atmega328 [package=dip]
  C1 = Ceramic Capacitor [capacitance=100nF voltage=16V package="200 mil [THT, multilayer]"]
  C3 = Ceramic Capacitor [capacitance=22pF package="200 mil [THT, multilayer]"]
  LED1 = LED - 5mm [color="Red (633nm)" package="5 mm [THT]"]
  C2 = Ceramic Capacitor [capacitance=22pF package="200 mil [THT, multilayer]"]
  Battery = Battery
  R3 = Resistor [tolerance=±5% resistance=270 package=THT]
  R1 = Resistor [tolerance=±5% resistance=10k package=THT]
  XTAL1 = Crystal [frequency="16 Mhz" package=THT]

nets:
  N1: IC1.RESET, R1.Pin_1
  N2: IC1.VCC, IC1.AVCC, C1.1, Battery.+, R1.Pin_0
  GND: IC1.GND, C1.0, C3.1, LED1.cathode, C2.1, Battery.-
  N3: IC1.XLAT1, C3.0, XTAL1.pin_0
  N4: IC1.XLAT2, C2.0, XTAL1.pin_1
  N5: IC1.D13, R3.Pin_1
  N6: LED1.anode, R3.Pin_0
