# Fritzing sketch ch_08_Protoshield (saved by Fritzing 0.9.1b)

parts:
  Protoshield = Arduino Prototyping Shield
  R1 = Resistor [tolerance=±5% resistance=220 package=THT]
  LED1 = LED - 5mm [color="Red (633nm)" package="5 mm [THT]"]

nets:
  N1: Protoshield.GND, Protoshield.N$64, LED1.cathode
  N2: Protoshield.D3, Protoshield.N$414, R1.Pin_0
  N3: Protoshield.N$88, Protoshield.N$243, R1.Pin_1, LED1.anode
