# Fritzing sketch ch_08_lighting_shield (saved by Fritzing 0.9.1b)
circuit board: 6.88566cm x 5.36311cm
breadboards: 1

parts:
  Q1 = Basic FET N-Channel [package="TO220 [THT]"]
  R1 = Resistor [tolerance=±5% resistance=1k package=THT]
  Q2 = Basic FET N-Channel [package="TO220 [THT]"]
  R2 = Resistor [tolerance=±5% resistance=1k package=THT]
  Q3 = Basic FET N-Channel [package="TO220 [THT]"]
  Lamp_C = Screw terminal - 2 pins [package=THT]
  R3 = Resistor [tolerance=±5% resistance=1k package=THT]
  part = Arduino Uno (Rev3)
  Lamp_A = screw terminal, 2 pins
  Lamp_B = Screw terminal - 2 pins [package=THT]

nets:
  N1: Q1.gate, R1.Pin_1
  N2: Q1.drain, Lamp_A.pin2
  N3: Q1.source, Q2.source, Q3.source, part.GND
  N4: R1.Pin_0, part.D11_PWM/MOSI
  N5: Q2.gate, R2.Pin_1
  N6: Q2.drain, Lamp_B.pin2
  N7: R2.Pin_0, part.D10_PWM/SS
  N8: Q3.gate, R3.Pin_1
  N9: Q3.drain, Lamp_C.pin2
  N10: Lamp_C.pin1, part.VIN, Lamp_A.pin1, Lamp_B.pin1
  N11: R3.Pin_0, part.D9_PWM
