# Fritzing sketch ch_10_Chicken_Door (saved by Fritzing 0.8.4b)
stripboards: 1

parts:
  Q1 = Basic FET N-Channel [package="TO220 [THT]"]
  Part1 = Arduino Pro Mini v13
  D3 = Rectifier Diode [part_number=1N4001 package="300 mil [THT]"]
  U1 = LIPO-2000mAh [package=lipo-2000]
  D4 = SOLAR-IXYS [package=solarbit-12x1]
  R1 = Resistor [tolerance=±5% resistance=10k package=THT]
  R2 = Resistor [tolerance=±5% resistance=10k package=THT]
  S1 = Toggle Switch [package=THT]
  J2 = Basic Servo

nets:
  N1: Q1.gate, Part1.D8
  N2: Q1.drain, J2.gnd
  N3: Q1.source, Part1.GND, U1.-, D4.A, R2.Pin_0
  N4: Part1.RAW, D3.cathode, S1.COM, J2.vcc
  N5: Part1.A0, R1.Pin_1, R2.Pin_1
  N6: Part1.D10_PWM/SS, J2.pulse
  N7: D3.anode, D4.C, R1.Pin_0
  N8: U1.+, S1.L2
