# Fritzing sketch ch_10_breakout_board (saved by Fritzing 0.9.1b)
circuit board: 2.19506cm x 2.13861cm
breadboards: 1

parts:
  IC1 = SO08 [chip_label=IC part_number=L9110 package=SO]
  J1 = male pin header, 6 pins [form="♂ (male)"]
  C1 = Ceramic Capacitor [capacitance=100nF voltage=16V package="0805 [SMD, multilayer]"]

nets:
  N1: IC1.1, J1.pin4
  N2: IC1.2, IC1.3, J1.pin1, C1.1
  N3: IC1.4, J1.pin5
  N4: IC1.5, IC1.8, J1.pin6, C1.0
  N5: IC1.6, J1.pin3
  N6: IC1.7, J1.pin2

notes:
  Vcc
  IB
  IA
  OB
  OA
  GND
  L9110 Breakout
  VCC
