# Fritzing sketch cycle_lamp_example_bat_on_back (saved by Fritzing 0.9.1b)
circuit board: 9.98037cm x 3.6979cm
breadboards: 1

parts:
  IC1 = General purpose bipolar Timer [package=dil-08]
  R1 = Resistor [tolerance=±5% resistance=10k package=THT]
  R2 = Resistor [tolerance=±5% resistance=10k package=THT]
  C1 = Electrolytic Capacitor [capacitance=10µF voltage=16V package="100 mil [THT, electrolytic]"]
  C2 = Ceramic Capacitor [capacitance=100nF package="100 mil [THT, multilayer]"]
  R3 = Resistor [tolerance=±5% resistance=68 package=THT]
  R4 = Resistor [tolerance=±5% resistance=68 package=THT]
  R5 = Resistor [tolerance=±5% resistance=68 package=THT]
  R6 = Resistor [tolerance=±5% resistance=68 package=THT]
  LED1 = LED - 5mm [color="Red (633nm)" package="5 mm [THT]"]
  LED2 = LED - 5mm [color="Red (633nm)" package="5 mm [THT]"]
  LED3 = LED - 5mm [color="Red (633nm)" package="5 mm [THT]"]
  LED4 = LED - 5mm [color="Red (633nm)" package="5 mm [THT]"]
  S1 = Toggle Switch [package=THT]
  BAT2 = BATTERY-2 [package=battery-aaa]
  BAT1 = BATTERY-2 [package=battery-aaa]

nets:
  GND: IC1.GND, C1.-, C2.0, BAT2.-1, BAT2.-2
  N1: IC1.TRI, IC1.TRE, R2.Pin_0, C1.+
  N2: IC1.OUT, LED1.cathode, LED2.cathode, LED3.cathode, LED4.cathode
  3V: IC1._RES, IC1.VCC+, R1.Pin_1, R3.Pin_1, R4.Pin_1, R5.Pin_1, R6.Pin_1, S1.L2
  N3: IC1.CON, C2.1
  N4: IC1.DIS, R1.Pin_0, R2.Pin_1
  N5: R3.Pin_0, LED1.anode
  N6: R4.Pin_0, LED2.anode
  N7: R5.Pin_0, LED3.anode
  N8: R6.Pin_0, LED4.anode
  N9: S1.COM, BAT1.+1, BAT1.+2
  N10: BAT2.+1, BAT2.+2, BAT1.-1, BAT1.-2

notes:
  Rear Cycle Lamp, Rear cycle light project from the book Fritzing for Inventors. , 1.0c
  Cycle Lamp v1.0a
