# Fritzing sketch cycle_lamp_example_smd (saved by Fritzing 0.9.1b)
circuit board: 10cm x 5cm
breadboards: 1

parts:
  BAT1 = BATTERY-2 [package=battery-aaa]
  BAT2 = BATTERY-2 [package=battery-aaa]
  S1 = Toggle Switch [package=THT]
  C1 = Electrolytic Capacitor [capacitance=10µF voltage=16V package="0405 [SMD, electrolytic]"]
  IC1 = 555 Timer [package="SO8 [SMD]"]
  R1 = Resistor [tolerance=±5% resistance=10k package="0805 [SMD]"]
  R2 = Resistor [tolerance=±5% resistance=10k package="0805 [SMD]"]
  R3 = Resistor [tolerance=±5% resistance=68 package="0805 [SMD]"]
  R4 = Resistor [tolerance=±5% resistance=68 package="0805 [SMD]"]
  R5 = Resistor [tolerance=±5% resistance=68 package="0805 [SMD]"]
  R6 = Resistor [tolerance=±5% resistance=68 package="0805 [SMD]"]
  C2 = Ceramic Capacitor [capacitance=100nF package="0805 [SMD, multilayer]"]
  LED1 = smd LED [color="Red (633nm)" package="1206 [SMD]"]
  LED2 = smd LED [color="Red (633nm)" package="1206 [SMD]"]
  LED3 = smd LED [color="Red (633nm)" package="1206 [SMD]"]
  LED4 = smd LED [color="Red (633nm)" package="1206 [SMD]"]

nets:
  N1: BAT1.-1, BAT1.-2, BAT2.+1, BAT2.+2
  N2: BAT1.+1, BAT1.+2, S1.COM
  GND: BAT2.-1, BAT2.-2, C1.-, IC1.Pin_1, C2.0
  3V: S1.L2, IC1.Pin_4, IC1.Pin_8, R1.Pin_1, R3.Pin_1, R4.Pin_1, R5.Pin_1, R6.Pin_1
  N3: C1.+, IC1.Pin_2, IC1.Pin_6, R2.Pin_0
  N4: IC1.Pin_3, LED1.cathode, LED2.cathode, LED3.cathode, LED4.cathode
  N5: IC1.Pin_5, C2.1
  N6: IC1.Pin_7, R1.Pin_0, R2.Pin_1
  N7: R3.Pin_0, LED1.anode
  N8: R4.Pin_0, LED2.anode
  N9: R5.Pin_0, LED3.anode
  N10: R6.Pin_0, LED4.anode

notes:
  Rear Cycle Lamp, Rear cycle light project from the book Fritzing for Inventors. , 1.0c
  Cycle Lamp v1.0a
